// Logisim project Calculadora Digital.circ as structural Verilog
module main (
  input  in_1,
  input  [3:0] A,
  input  [3:0] B,
  input  Registrar,
  input  Limpar,
  input  in_6,
  input  [1:0] in_7,
  input  in_8,
  output [7:0] out_9
);

  wire bcd_to_7_segment_decoder_2_p1, bcd_to_7_segment_decoder_3_p1, binary_to_bcd_converter_1_p2;
  wire [3:0] multiplexador_1_out_4, register_1_q, register_2_q;
  wire [7:0] register_3_q;

  Register #(.width(4)) register_1 (
    .D(multiplexador_1_out_4), .clk(Registrar), .Q(register_1_q), .clr(Limpar));  // open: en
  multiplexador multiplexador_1 (.in_1(in_1), .in_2(A), .in_3(out_9), .out_4(multiplexador_1_out_4));
  Register #(.width(4)) register_2 (.D(B), .clk(Registrar), .Q(register_2_q), .clr(Limpar));  // open: en
  Register register_3 (.D(out_9), .clk(in_6), .Q(register_3_q), .clr(in_8));  // open: en
  calculadora calculadora_1 (.A(register_1_q), .B(register_2_q), .Opera_o_60c103be(in_7), .Resultado(out_9));
  _7_Segment_Display aaaa ();  // open: g, f, a, b, e, d, c, dp
  // BCD_to_7_Segment_decoder bcd_to_7_segment_decoder_1: pin names not known
  _7_Segment_Display u_7_segment_display_1 ();  // open: g, f, a, b, e, d, c, dp
  // BCD_to_7_Segment_decoder bcd_to_7_segment_decoder_2: pin names not known; wires that end beside it: bcd_to_7_segment_decoder_2_p1
  // Binary_to_BCD_converter #(.binvalue(8)) binary_to_bcd_converter_1: pin names not known; wires that end beside it: register_3_q, binary_to_bcd_converter_1_p2, binary_to_bcd_converter_1_p2, bcd_to_7_segment_decoder_2_p1
  _7_Segment_Display u_7_segment_display_2 ();  // open: g, f, a, b, e, d, c, dp
  // BCD_to_7_Segment_decoder bcd_to_7_segment_decoder_3: pin names not known; wires that end beside it: bcd_to_7_segment_decoder_3_p1, bcd_to_7_segment_decoder_3_p1
endmodule

module somador (
  input  [3:0] A,
  input  [3:0] B,
  output Carry,
  output [3:0] S
);

  wire meio_somador_1_carry;

  meio_somador meio_somador_1 (.A(A[0]), .B(B[0]), .Soma(S[0]), .Carry(meio_somador_1_carry));
  somador_3_bits_08e3cf9d somador_3_bits (
    .A1(A[1]), .A2(A[2]), .A3(A[3]), .B1(B[1]), .B2(B[2]), .B3(B[3]),
    .Carry_in_6616bdd5(meio_somador_1_carry), .Carry(Carry), .S1(S[1]), .S2(S[2]), .S3(S[3]));
endmodule

module multiplexador (
  input  in_1,
  input  [3:0] in_2,
  input  [7:0] in_3,
  output [3:0] out_4
);

  wire [3:0] and_1_out, and_2_out, not_1_out;
  wire [3:3] comparator_1_lt;

  Comparator #(.mode("unsigned")) comparator_1 (.a(in_3), .b(8'h10), .lt(comparator_1_lt[3]));  // open: gt, eq
  assign and_1_out = in_2 & {4{in_1}};  // AND_Gate and_1, 4 bits wide
  assign not_1_out = ~{4{in_1}};  // NOT_Gate not_1, 4 bits wide
  assign and_2_out = not_1_out & in_3[3:0] & {4{comparator_1_lt[3]}};  // AND_Gate and_2, 4 bits wide
  assign out_4 = and_1_out | and_2_out;  // OR_Gate or_1, 4 bits wide
endmodule

module meio_somador (
  input  A,
  input  B,
  output Soma,
  output Carry
);

  xor xor_1 (Soma, A, B);
  and and_1 (Carry, A, B);
endmodule

module subtrator (
  input  [3:0] A,
  input  [3:0] B,
  output Carry,
  output [3:0] S
);

  wire not_1_out, not_2_out, not_3_out, not_4_out, somador_completo_1_carry;

  somador_completo somador_completo_1 (
    .A(A[0]), .B(not_1_out), .Cin(1'b1), .Soma(S[0]), .Carry(somador_completo_1_carry));
  not not_1 (not_1_out, B[0]);
  not not_2 (not_2_out, B[1]);
  not not_3 (not_3_out, B[2]);
  not not_4 (not_4_out, B[3]);
  somador_3_bits_08e3cf9d somador_3_bits_08e3cf9d_1 (
    .A1(A[1]), .A2(A[2]), .A3(A[3]), .B1(not_2_out), .B2(not_3_out), .B3(not_4_out),
    .Carry_in_6616bdd5(somador_completo_1_carry), .Carry(Carry), .S1(S[1]), .S2(S[2]), .S3(S[3]));
endmodule

module somador_completo (
  input  A,
  input  B,
  input  Cin,
  output Soma,
  output Carry
);

  wire and_1_out, and_2_out, xor_1_out;

  xor xor_1 (xor_1_out, A, B);
  xor xor_2 (Soma, Cin, xor_1_out);
  and and_1 (and_1_out, xor_1_out, Cin);
  and and_2 (and_2_out, A, B);
  or or_1 (Carry, and_1_out, and_2_out);
endmodule

module somador_3_bits_08e3cf9d (
  input  A1,
  input  A2,
  input  A3,
  input  B1,
  input  B2,
  input  B3,
  input  Carry_in_6616bdd5,
  output Carry,
  output S1,
  output S2,
  output S3
);

  wire somador_completo_1_carry, somador_completo_2_carry;

  somador_completo somador_completo_1 (
    .A(A1), .B(B1), .Cin(Carry_in_6616bdd5), .Soma(S1), .Carry(somador_completo_1_carry));
  somador_completo somador_completo_2 (
    .A(A2), .B(B2), .Cin(somador_completo_1_carry), .Soma(S2), .Carry(somador_completo_2_carry));
  somador_completo somador_completo_3 (.A(A3), .B(B3), .Cin(somador_completo_2_carry), .Soma(S3), .Carry(Carry));
endmodule

module comparador (
  input  B,
  input  [3:0] A,
  output [3:0] out_3
);

  and and_1 (out_3[3], B, A[3]);
  and and_2 (out_3[2], B, A[2]);
  and and_3 (out_3[1], B, A[1]);
  and and_4 (out_3[0], B, A[0]);
endmodule

module multiplicador (
  input  [3:0] B,
  input  [3:0] A,
  output [7:0] out_3
);

  wire [3:0] comparador_2_out_3, comparador_3_out_3, comparador_4_out_3;
  wire [3:1] comparador_1_out_3, somador_1_s, somador_2_s;
  wire [3:3] somador_1_carry, somador_2_carry;

  comparador comparador_1 (.B(B[0]), .A(A), .out_3({comparador_1_out_3, out_3[0]}));
  comparador comparador_2 (.B(B[1]), .A(A), .out_3(comparador_2_out_3));
  comparador comparador_3 (.B(B[2]), .A(A), .out_3(comparador_3_out_3));
  comparador comparador_4 (.B(B[3]), .A(A), .out_3(comparador_4_out_3));
  somador somador_1 (
    .A({1'b0, comparador_1_out_3}), .B(comparador_2_out_3), .Carry(somador_1_carry[3]),
    .S({somador_1_s, out_3[1]}));
  somador somador_2 (
    .A({somador_1_carry[3], somador_1_s}), .B(comparador_3_out_3), .Carry(somador_2_carry[3]),
    .S({somador_2_s, out_3[2]}));
  somador somador_3 (.A({somador_2_carry[3], somador_2_s}), .B(comparador_4_out_3), .Carry(out_3[7]), .S(out_3[6:3]));
endmodule

module divisor (
  input  [3:0] A,
  input  [3:0] B,
  output [3:0] S
);

  wire [3:0] and_1_out, and_2_out, or_1_out, register_1_q, subtrator_1_s;
  wire [3:3] clock_1_out;

  Clock clock_1 (.out(clock_1_out[3]));
  assign and_1_out = register_1_q & {4{clock_1_out[3]}};  // AND_Gate and_1, 4 bits wide
  assign and_2_out = {4{clock_1_out[3]}} & A;  // AND_Gate and_2, 4 bits wide
  assign or_1_out = and_1_out | and_2_out;  // OR_Gate or_1, 4 bits wide
  Register #(.width(4)) register_1 (.D(subtrator_1_s), .clk(clock_1_out[3]), .Q(register_1_q));  // open: en, clr
  subtrator subtrator_1 (.A(or_1_out), .B(B), .S(subtrator_1_s));  // open: Carry
  contador contador_1 (.CLK(clock_1_out[3]), .S(S));
endmodule

module contador (
  input  CLK,
  output [3:0] S
);

  wire and_1_out, and_2_out;

  T_Flip_Flop t_ff_1 (.T(1'b1), .clk(CLK), .Q(S[3]));  // open: Qn, reset, preset
  T_Flip_Flop t_ff_2 (.T(S[3]), .clk(CLK), .Q(S[2]));  // open: Qn, reset, preset
  and and_1 (and_1_out, S[3], S[2]);
  T_Flip_Flop t_ff_3 (.T(and_1_out), .clk(CLK), .Q(S[1]));  // open: Qn, reset, preset
  buf and_2 (and_2_out, S[1]);  // AND_Gate
  T_Flip_Flop t_ff_4 (.T(and_2_out), .clk(CLK), .Q(S[0]));  // open: Qn, reset, preset
endmodule

module calculadora (
  input  [3:0] A,
  input  [3:0] B,
  input  [1:0] Opera_o_60c103be,
  output [7:0] Resultado
);

  wire [3:0] divisor_1_s, somador_1_s, subtrator_1_s;
  wire [4:4] somador_1_carry;
  wire [7:0] and_1_out, and_2_out, and_3_out, and_4_out, multiplicador_1_out_3, not_1_out, not_2_out,
       not_3_out, not_4_out;

  somador somador_1 (.A(A), .B(B), .Carry(somador_1_carry[4]), .S(somador_1_s));
  subtrator subtrator_1 (.A(A), .B(B), .S(subtrator_1_s));  // open: Carry
  multiplicador multiplicador_1 (.B(A), .A(B), .out_3(multiplicador_1_out_3));
  divisor divisor_1 (.A(A), .B(B), .S(divisor_1_s));
  assign not_1_out = ~{8{Opera_o_60c103be[0]}};  // NOT_Gate not_1, 8 bits wide
  assign and_1_out = {3'b000, somador_1_carry[4], somador_1_s} & not_1_out & not_2_out;  // AND_Gate and_1, 8 bits wide
  assign not_2_out = ~{8{Opera_o_60c103be[1]}};  // NOT_Gate not_2, 8 bits wide
  assign and_2_out = {4'b0000, subtrator_1_s} & {8{Opera_o_60c103be[0]}} & not_3_out;  // AND_Gate and_2, 8 bits wide
  assign not_3_out = ~{8{Opera_o_60c103be[1]}};  // NOT_Gate not_3, 8 bits wide
  assign not_4_out = ~{8{Opera_o_60c103be[0]}};  // NOT_Gate not_4, 8 bits wide
  assign and_3_out = multiplicador_1_out_3 & not_4_out & {8{Opera_o_60c103be[1]}};  // AND_Gate and_3, 8 bits wide
  assign and_4_out = {4'b0000, divisor_1_s} & {8{Opera_o_60c103be[0]}} & {8{Opera_o_60c103be[1]}};  // AND_Gate and_4, 8 bits wide
  assign Resultado = and_1_out | and_2_out | and_3_out | and_4_out;  // OR_Gate or_1, 8 bits wide
endmodule

module decodificador_BCD (
  input  [7:0] Entrada,
  output [3:0] S0,
  output [3:0] S1,
  output [3:0] S2
);

  add3 add3_1 ();  // open: in_1, out_2
endmodule

module decodificador_7_seg (
  input  [3:0] Entrada,
  output [6:0] S
);
endmodule

module add3 (
  input  [3:0] in_1,
  output [3:0] out_2
);

  wire and_1_out, and_2_out, and_3_out, and_4_out, and_5_out, and_6_out, and_7_out, and_8_out, and_9_out,
       and_10_out, not_1_out, not_3_out, not_4_out, not_8_out;

  not not_1 (not_1_out, in_1[3]);
  // NOT_Gate not_2 has open pins: in=in_1[2], out=open
  and and_1 (and_1_out, not_1_out, in_1[0]);
  and and_2 (and_2_out, in_1[3], not_3_out);
  not not_3 (not_3_out, in_1[0]);
  and and_3 (and_3_out, in_1[2], not_4_out);
  not not_4 (not_4_out, in_1[0]);
  // NOT_Gate not_5 has open pins: in=in_1[2], out=open
  // AND_Gate and_4 has open pins: out=and_4_out
  // AND_Gate and_5 has open pins: out=and_5_out
  // AND_Gate and_6 has open pins: out=and_6_out
  // NOT_Gate not_6 has open pins: in=in_1[0], out=open
  // NOT_Gate not_7 has open pins: in=in_1[1], out=open
  and and_7 (and_7_out, in_1[2], not_8_out);
  not not_8 (not_8_out, in_1[0]);
  // AND_Gate and_8 has open pins: out=and_8_out
  // AND_Gate and_9 has open pins: out=and_9_out
  // AND_Gate and_10 has open pins: out=and_10_out
  or or_1 (out_2[0], and_1_out, and_3_out);
  or or_2 (out_2[1], and_4_out, and_6_out);
  // OR_Gate or_3 has open pins: out=out_2[2]
  or or_4 (out_2[3], and_9_out, and_10_out);
endmodule
